# Fritzing sketch stabilizer_nano (saved by Fritzing 0.9.4)
breadboards: 1
perfboards: 1

parts:
  Part3 = InvenSense MPU6050
  Part2 = Arduino Nano (Rev3.0)
  J2 = Basic Servo
  J3 = Basic Servo
  U1 = LIPO-2000mAh [package=lipo-2000]
  Part5 = Arduino Nano (Rev3.0)
  Part6 = InvenSense MPU6050
  J4 = Dagu DGServo 9g header (male) [package=THT]
  J5 = Dagu DGServo 9g header (male) [package=THT]
  J6 = Dagu DGServo 9g header (male) [package=THT]
  J7 = Dagu DGServo 9g header (male) [package=THT]
  J8 = Dagu DGServo 9g header (male) [package=THT]
  Mod1 = flyskyr6b
  J9 = Basic Servo  # not connected
  J10 = Basic Servo  # not connected

nets:
  VCC: Part3.VCC, Part2.VIN, J2.vcc, J3.vcc, U1.+
  GND: Part3.GND, Part2.GND, J2.gnd, J3.gnd, U1.-
  N1: Part3.SCL, Part2.A5
  N2: Part3.SDA, Part2.A4
  N3: Part3.INT, Part2.D2
  N4: Part2.D5, J3.pulse
  N5: Part2.D6, J2.pulse
  GND_2: Part5.GND, J4.pulse, Mod1.connector14, Mod1.GND
  N6: Part5.D2, Part6.INT
  N7: Part5.D8, J5.pulse
  N8: Part5.D9, J6.pulse
  N9: Part5.D10, J7.pulse
  N10: Part5.D11/MOSI, J8.pulse
  N11: Part5.A5, Part6.SCL
  N12: Part5.A4, Part6.SDA
  VCC_2: Part6.VCC, J4.Vcc, Mod1.VCC, Mod1.BAT+
  N13: J5.Vcc, Mod1.CH1
  N14: J6.Vcc, Mod1.CH2

custom parts:
  flyskyr6b: flysky r6b 6ch rc receiver module. Pcb view is 3*7 header pins, 3 female headers will let the board plug in to the receiver, or connect via wires as you choose.
