# Fritzing sketch stabilizer_nano (saved by Fritzing 0.9.4)
breadboards: 1

parts:
  Part3 = InvenSense MPU6050
  Part2 = Arduino Nano (Rev3.0)
  J3 = Basic Servo
  Mod1 = flyskyr6b
  J4 = Basic Servo
  J5 = Dagu DGServo 9g header connector (female) [package=THT]  # not connected

nets:
  VCC: Part3.VCC, Part2.VIN, J3.vcc, J4.vcc
  GND: Part3.GND, Part2.GND, J3.gnd, J4.gnd
  N1: Part3.SCL, Part2.A5
  N2: Part3.SDA, Part2.A4
  N3: Part3.INT, Part2.D2
  N4: Part2.D5, J3.pulse
  N5: Part2.D6, J4.pulse
  N6: Part2.D8, Mod1.CH1
  N7: Part2.D9, Mod1.CH2
  N8: Part2.D10, Mod1.CH3
  N9: Part2.D11/MOSI, Mod1.CH5

custom parts:
  flyskyr6b: flysky r6b 6ch rc receiver module. Pcb view is 3*7 header pins, 3 female headers will let the board plug in to the receiver, or connect via wires as you choose.
